# Fritzing sketch BobbisDualColorLed (saved by Fritzing 1.0.4)
perfboards: 1

parts:
  LED1 = DUO LED RG [package="5 mm [THT]"]
  D1 = Diode [package=diode-1n4148]
  R1 = Resistor [tolerance=±5% power=0.25W resistance=470 package=THT]
  J1 = male pin header, 3 pins [form="♂ (male)"]

nets:
  N1: LED1.red_anode, D1.C
  N2: LED1.common_cathode, R1.Pin_0
  N3: LED1.green_anode, J1.pin3
  N4: D1.A, J1.pin1
  N5: R1.Pin_1, J1.pin2

notes:
  5V
  GND
  IN
